# Fritzing sketch turkey_temp_tracker (saved by Fritzing 0.9.3b)
breadboards: 1

parts:
  C1 = Electrolytic Capacitor [capacitance=1µF package="100 mil [THT, electrolytic]"]
  C3 = Electrolytic Capacitor [capacitance=1µF package="100 mil [THT, electrolytic]"]
  R1 = Resistor [tolerance=±5% resistance=10k package=THT]
  R2 = Resistor [tolerance=±5% resistance=10k package=THT]
  R3 = Temperature Sensor (Thermistor) [thermistor_type=NTC package=THT]
  R4 = Temperature Sensor (Thermistor) [thermistor_type=NTC package=THT]

nets:
  N1: C1.-, C3.-, R3.pin_1, R4.pin_0
  N2: C1.+, R2.Pin_0, R3.pin_0
  N3: C3.+, R1.Pin_0, R4.pin_1
  N4: R1.Pin_1, R2.Pin_1

notes:
  THERM 1
  THERM 2
